# Fritzing sketch FRİTZİNG (saved by Fritzing 0.9.10b)
breadboards: 1

parts:
  R1 = Resistor [tolerance=±0.05% power=0.25W resistance=2000 package=THT]
  R2 = Resistor [tolerance=±0.05% power=0.25 resistance=3000 package=THT]
  R3 = Resistor [tolerance=±0.05% power=0.25 resistance=5000 package=THT]
  R4 = Resistor [tolerance=±0.05% power=0.25 resistance=10000 package=THT]
  R5 = Resistor [tolerance=±0.05% power=0.25 resistance=20000 package=THT]
  R7 = Resistor [tolerance=±0.05% power=0.25 resistance=7000 package=THT]
  R8 = Resistor [tolerance=±0.05% power=0.25 resistance=8000 package=THT]
  V1 = DC Power [voltage=15V]
  R6 = Resistor [tolerance=±0.05% power=0.25 resistance=5000 package=THT]
  VM1 = Multimeter (DC Voltage)
  P1 = Multimeter straight black probe
  P2 = Multimeter straight red probe

nets:
  N1: R1.Pin_0, R4.Pin_0, V1.V+
  N2: R1.Pin_1, R2.Pin_0
  N3: R2.Pin_1, R3.Pin_0, VM1.V_Probe, P2.Probe_tip, P2.Probe_meter_end
  N4: R4.Pin_1, R5.Pin_1, R6.Pin_0
  GND: R5.Pin_0, R8.Pin_1, V1.V-, VM1.COM_Probe, P1.Probe_tip, P1.Probe_meter_end
  N5: R7.Pin_0, R6.Pin_1
  N6: R7.Pin_1, R8.Pin_0
