# Fritzing sketch Fritzing (saved by Fritzing 0.9.10b)
breadboards: 1

parts:
  R1 = Resistor [tolerance=±0.05% resistance=5k package="0805 [SMD]"]
  R2 = Resistor [tolerance=±0.05% resistance=15k package="0805 [SMD]"]
  R3 = Resistor [tolerance=±0.05% resistance=10k package="0805 [SMD]"]
  R4 = Resistor [tolerance=±0.05% resistance=20k package="0805 [SMD]"]
  V1 = DC Power [voltage=15V]
  C1 = Ceramic Capacitor [capacitance=0.5µF voltage=0V package="100 mil [THT, multilayer]"]
  VM1 = Multimeter (DC Voltage)
  S1 = SWITCH-MOMENTARY-2 [mn=1 mpn=10 package=tactile_switch_tall]

nets:
  N1: R1.Pin_0, V1.V+
  N2: R1.Pin_1, S1.1
  N3: R2.Pin_0, V1.V-
  N4: R2.Pin_1, R3.Pin_0, C1.1, VM1.V_Probe, S1.2
  N5: R3.Pin_1, R4.Pin_1
  N6: R4.Pin_0, C1.0, VM1.COM_Probe
